// Logisim project CombinationalLogic.circ as structural Verilog: 2 circuits, main circuit main
module main (
  input  in_1,
  input  in_2,
  input  in_3,
  input  [3:0] in_4,
  input  [3:0] in_5,
  output out_6,
  output out_7,
  output out_8,
  output out_9,
  output out_10,
  output out_11,
  output out_12,
  output out_13
);

  wire and_1_out, and_2_out, and_3_out, and_4_out, and_5_out, and_6_out, and_7_out, and_8_out,
       decoder2_4_1_out_3, decoder2_4_1_out_4, decoder2_4_1_out_5, decoder2_4_1_out_6, decoder2_4_2_out_3,
       decoder2_4_2_out_4, decoder2_4_2_out_5, decoder2_4_2_out_6, decoder2_4_3_out_3, decoder2_4_3_out_4,
       decoder2_4_3_out_5, decoder2_4_3_out_6, decoder2_4_4_out_3, decoder2_4_4_out_4, decoder2_4_4_out_5,
       decoder2_4_4_out_6, decoder_1_out0, decoder_1_out1, decoder_1_out2, decoder_1_out3, decoder_1_out4,
       decoder_1_out5, decoder_1_out6, decoder_1_out7, decoder_1_out8, decoder_1_out9, decoder_1_out10,
       decoder_1_out11, decoder_1_out12, decoder_1_out13, decoder_1_out14, decoder_1_out15, decoder_2_out0,
       decoder_2_out1, decoder_2_out2, decoder_2_out3, decoder_2_out4, decoder_2_out5, decoder_2_out6,
       decoder_2_out7, decoder_2_out8, decoder_2_out9, decoder_2_out10, decoder_2_out11, decoder_2_out12,
       decoder_2_out13, decoder_2_out14, decoder_2_out15, not_1_out, not_2_out, not_3_out, or_1_out,
       or_2_out, or_3_out, or_4_out, or_5_out, or_6_out, or_7_out, or_8_out, or_9_out, or_10_out, or_11_out,
       or_12_out, or_13_out, or_14_out, or_15_out;

  not not_1 (not_1_out, in_1);
  not not_2 (not_2_out, in_2);
  not not_3 (not_3_out, in_3);
  Decoder #(.enable("false"), .select(4)) decoder_1 (
    .out0(decoder_1_out0), .out1(decoder_1_out1), .out2(decoder_1_out2), .out3(decoder_1_out3),
    .out4(decoder_1_out4), .out5(decoder_1_out5), .out6(decoder_1_out6), .out7(decoder_1_out7),
    .out8(decoder_1_out8), .out9(decoder_1_out9), .out10(decoder_1_out10), .out11(decoder_1_out11),
    .out12(decoder_1_out12), .out13(decoder_1_out13), .out14(decoder_1_out14), .out15(decoder_1_out15),
    .sel(in_4));
  or or_1 (or_1_out, decoder_1_out15, decoder_1_out14, decoder_1_out13, decoder_1_out12, decoder_1_out11, decoder_1_out10);
  decoder2_4 decoder2_4_1 (
    .in_1(in_1), .in_2(not_2_out), .out_3(decoder2_4_1_out_3), .out_4(decoder2_4_1_out_4),
    .out_5(decoder2_4_1_out_5), .out_6(decoder2_4_1_out_6));
  decoder2_4 decoder2_4_2 (
    .in_1(not_1_out), .in_2(in_2), .out_3(decoder2_4_2_out_3), .out_4(decoder2_4_2_out_4),
    .out_5(decoder2_4_2_out_5), .out_6(decoder2_4_2_out_6));
  decoder2_4 decoder2_4_3 (
    .in_1(in_2), .in_2(in_3), .out_3(decoder2_4_3_out_3), .out_4(decoder2_4_3_out_4),
    .out_5(decoder2_4_3_out_5), .out_6(decoder2_4_3_out_6));
  decoder2_4 decoder2_4_4 (
    .in_1(not_2_out), .in_2(not_3_out), .out_3(decoder2_4_4_out_3), .out_4(decoder2_4_4_out_4),
    .out_5(decoder2_4_4_out_5), .out_6(decoder2_4_4_out_6));
  and and_1 (and_1_out, decoder2_4_1_out_3, decoder2_4_2_out_6);
  and and_2 (and_2_out, decoder2_4_1_out_4, decoder2_4_2_out_5);
  and and_3 (and_3_out, decoder2_4_1_out_6, decoder2_4_2_out_3);
  and and_4 (and_4_out, decoder2_4_1_out_5, decoder2_4_2_out_4);
  and and_5 (and_5_out, decoder2_4_3_out_4, decoder2_4_4_out_5);
  and and_6 (and_6_out, decoder2_4_3_out_3, decoder2_4_4_out_6);
  and and_7 (and_7_out, decoder2_4_3_out_5, decoder2_4_4_out_4);
  and and_8 (and_8_out, decoder2_4_3_out_6, decoder2_4_4_out_3);
  or or_2 (or_2_out, decoder_1_out0, decoder_1_out2, decoder_1_out3, decoder_1_out9, decoder_1_out5, decoder_1_out6, decoder_1_out7, decoder_1_out8);
  or or_3 (or_3_out, decoder_1_out0, decoder_1_out1, decoder_1_out2, decoder_1_out3, decoder_1_out4, decoder_1_out8, decoder_1_out7, decoder_1_out9);
  or or_4 (or_4_out, decoder_1_out0, decoder_1_out1, decoder_1_out3, decoder_1_out4, decoder_1_out5, decoder_1_out6, decoder_1_out7, decoder_1_out8, decoder_1_out9);
  or or_5 (or_5_out, decoder_1_out0, decoder_1_out2, decoder_1_out3, decoder_1_out5, decoder_1_out6, decoder_1_out8, decoder_1_out9);
  or or_6 (or_6_out, decoder_1_out0, decoder_1_out2, decoder_1_out6, decoder_1_out8);
  or or_7 (or_7_out, decoder_1_out0, decoder_1_out4, decoder_1_out5, decoder_1_out6, decoder_1_out8, decoder_1_out9);
  or or_8 (or_8_out, decoder_1_out2, decoder_1_out3, decoder_1_out4, decoder_1_out5, decoder_1_out6, decoder_1_out8, decoder_1_out9);
  and and_9 (out_6, and_2_out, and_6_out);
  and and_10 (out_7, and_2_out, and_5_out);
  and and_11 (out_8, and_1_out, and_7_out);
  and and_12 (out_9, and_1_out, and_8_out);
  and and_13 (out_10, and_6_out, and_3_out);
  and and_14 (out_11, and_3_out, and_5_out);
  buf and_15 (out_12, and_7_out);  // AND_Gate
  and and_16 (out_13, and_4_out, and_8_out);
  _7_Segment_Display u_7_segment_display_1 (
    .g(or_8_out), .f(or_7_out), .a(or_2_out), .b(or_3_out), .e(or_6_out), .d(or_5_out), .c(or_4_out),
    .dp(or_1_out));
  Decoder #(.enable("false"), .select(4)) decoder_2 (
    .out0(decoder_2_out0), .out1(decoder_2_out1), .out2(decoder_2_out2), .out3(decoder_2_out3),
    .out4(decoder_2_out4), .out5(decoder_2_out5), .out6(decoder_2_out6), .out7(decoder_2_out7),
    .out8(decoder_2_out8), .out9(decoder_2_out9), .out10(decoder_2_out10), .out11(decoder_2_out11),
    .out12(decoder_2_out12), .out13(decoder_2_out13), .out14(decoder_2_out14), .out15(decoder_2_out15),
    .sel(in_5));
  or or_9 (or_9_out, decoder_2_out10, decoder_2_out12, decoder_2_out0, decoder_2_out2, decoder_2_out3, decoder_2_out9, decoder_2_out5, decoder_2_out6, decoder_2_out7, decoder_2_out8, decoder_2_out14, decoder_2_out15);
  or or_10 (or_10_out, decoder_2_out10, decoder_2_out0, decoder_2_out1, decoder_2_out2, decoder_2_out3, decoder_2_out4, decoder_2_out8, decoder_2_out7, decoder_2_out9, decoder_2_out13);
  or or_11 (or_11_out, decoder_2_out5, decoder_2_out10, decoder_2_out0, decoder_2_out1, decoder_2_out3, decoder_2_out4, decoder_2_out6, decoder_2_out7, decoder_2_out8, decoder_2_out9, decoder_2_out11, decoder_2_out13);
  or or_12 (or_12_out, decoder_2_out11, decoder_2_out12, decoder_2_out0, decoder_2_out2, decoder_2_out3, decoder_2_out5, decoder_2_out6, decoder_2_out8, decoder_2_out9, decoder_2_out13, decoder_2_out14);
  or or_13 (or_13_out, decoder_2_out10, decoder_2_out11, decoder_2_out12, decoder_2_out0, decoder_2_out2, decoder_2_out6, decoder_2_out8, decoder_2_out13, decoder_2_out14, decoder_2_out15);
  or or_14 (or_14_out, decoder_2_out10, decoder_2_out11, decoder_2_out0, decoder_2_out4, decoder_2_out5, decoder_2_out12, decoder_2_out6, decoder_2_out8, decoder_2_out9, decoder_2_out14, decoder_2_out15);
  or or_15 (or_15_out, decoder_2_out5, decoder_2_out10, decoder_2_out11, decoder_2_out2, decoder_2_out3, decoder_2_out4, decoder_2_out6, decoder_2_out8, decoder_2_out9, decoder_2_out13, decoder_2_out14, decoder_2_out15);
  _7_Segment_Display u_7_segment_display_2 (
    .g(or_15_out), .f(or_14_out), .a(or_9_out), .b(or_10_out), .e(or_13_out), .d(or_12_out), .c(or_11_out));  // open: dp

  // Notes on the sheet:
  //   七段数码管译码器1
  //   2-4译码器实现3-8译码器
  //   七段数码管译码器2
endmodule

module decoder2_4 (
  input  in_1,
  input  in_2,
  output out_3,
  output out_4,
  output out_5,
  output out_6
);

  wire not_1_out, not_2_out;

  not not_1 (not_1_out, in_1);
  not not_2 (not_2_out, in_2);
  and and_1 (out_3, not_1_out, not_2_out);
  and and_2 (out_4, not_1_out, in_2);
  and and_3 (out_5, in_1, not_2_out);
  and and_4 (out_6, in_1, in_2);

  // Notes on the sheet:
  //   2-4译码器
endmodule
