// Logisim project SequentialLogic.circ as structural Verilog: 1 circuit, main circuit main
module main (
  output out_1,
  output out_2,
  output Q,
  output nQ
);

  wire and_1_out, and_2_out, and_3_out, and_4_out, dipswitch_1_p1, dipswitch_2_p1;

  // DipSwitch #(.number(1)) dipswitch_1: pin names not known; wires that end beside it: dipswitch_1_p1
  // DipSwitch #(.number(1)) dipswitch_2: pin names not known; wires that end beside it: dipswitch_2_p1
  // DipSwitch #(.number(1)) dipswitch_3: pin names not known
  buf and_1 (and_1_out, dipswitch_1_p1);  // AND_Gate
  buf and_2 (and_2_out, dipswitch_1_p1);  // AND_Gate
  // DipSwitch #(.number(1)) dipswitch_4: pin names not known
  // DipSwitch #(.number(1)) dipswitch_5: pin names not known
  buf and_3 (and_3_out, dipswitch_2_p1);  // AND_Gate
  buf and_4 (and_4_out, dipswitch_2_p1);  // AND_Gate
  // DipSwitch #(.number(1)) dipswitch_6: pin names not known
  nor nor_1 (out_1, and_1_out, out_2);
  nor nor_2 (out_2, out_1, and_2_out);
  nand nand_1 (Q, and_3_out, nQ);
  nand nand_2 (nQ, Q, and_4_out);

  // Notes on the sheet:
  //   SR锁存器
  //   ~S~R锁存器
  //   R
  //   S
endmodule
